// Logisim project Semi_Soma.circ as structural Verilog: 4 circuits, main circuit main
module main (
  input  in_1,
  input  in_2,
  input  in_3,
  input  in_4,
  input  in_5,
  input  in_6,
  input  in_7,
  input  in_8,
  output out_9,
  output out_10,
  output out_11,
  output out_12,
  output out_13
);

  Soma_de_4_bits soma_de_4_bits_1 (
    .in_2(in_1), .in_3(in_2), .in_4(in_3), .in_5(in_4), .in_6(in_5), .in_7(in_6), .in_8(in_7), .in_9(in_8),
    .in_1(1'b0), .out_14(out_13), .out_10(out_9), .out_11(out_10), .out_12(out_11), .out_13(out_12));
endmodule

module Soma_de_1_Bit (
  input  in_1,
  input  in_2,
  input  in_3,
  output S0,
  output Carry_out
);

  wire and_1_out, and_2_out, xor_1_out;

  xor xor_1 (xor_1_out, in_2, in_3);
  and and_1 (and_1_out, in_3, in_2);
  xor xor_2 (S0, in_1, xor_1_out);
  and and_2 (and_2_out, in_1, xor_1_out);
  or or_1 (Carry_out, and_2_out, and_1_out);
endmodule

module Soma_de_2_bits (
  input  in_1,
  input  in_2,
  input  in_3,
  input  in_4,
  input  in_5,
  output out_6,
  output out_7,
  output out_8
);

  wire soma_de_1_bit_1_carry_out;

  Soma_de_1_Bit soma_de_1_bit_1 (
    .in_2(in_2), .in_3(in_4), .in_1(in_1), .Carry_out(soma_de_1_bit_1_carry_out), .S0(out_6));
  Soma_de_1_Bit soma_de_1_bit_2 (
    .in_2(in_3), .in_3(in_5), .in_1(soma_de_1_bit_1_carry_out), .Carry_out(out_8), .S0(out_7));
endmodule

module Soma_de_4_bits (
  input  in_1,
  input  in_2,
  input  in_3,
  input  in_4,
  input  in_5,
  input  in_6,
  input  in_7,
  input  in_8,
  input  in_9,
  output out_10,
  output out_11,
  output out_12,
  output out_13,
  output out_14
);

  wire soma_de_2_bits_1_out_8;

  Soma_de_2_bits soma_de_2_bits_1 (
    .in_2(in_2), .in_3(in_6), .in_4(in_3), .in_5(in_7), .in_1(in_1), .out_8(soma_de_2_bits_1_out_8),
    .out_6(out_10), .out_7(out_11));
  Soma_de_2_bits soma_de_2_bits_2 (
    .in_2(in_4), .in_3(in_8), .in_4(in_5), .in_5(in_9), .in_1(soma_de_2_bits_1_out_8), .out_8(out_14),
    .out_6(out_12), .out_7(out_13));
endmodule
